// Logisim project control-logic.circ as structural Verilog: 1 circuit, main circuit control_logic
module control_logic (
  input  [31:0] inst,
  input  BrEq,
  input  BrLt,
  output PCSel,
  output RegWEn,
  output [2:0] ImmSel,
  output BrUn,
  output ASel,
  output BSel,
  output [3:0] ALUSel,
  output MemRW,
  output [1:0] WBSel,
  output CSRSel,
  output CSRWen,
  output [3:0] Write_Enable,
  output [1:0] Load_Type
);

  wire and_1_out, and_2_out, and_3_out, and_4_out, and_5_out, and_6_out, and_7_out, and_11_out, and_13_out,
       and_15_out, and_17_out, and_18_out, comparator_1_eq, comparator_2_eq, comparator_3_eq,
       comparator_4_eq, comparator_5_eq, comparator_6_eq, comparator_7_eq, comparator_8_eq, comparator_9_eq,
       comparator_10_eq, comparator_11_eq, comparator_12_eq, comparator_13_eq, comparator_14_eq,
       comparator_15_eq, comparator_16_eq, comparator_18_eq, comparator_20_eq, comparator_21_eq,
       comparator_22_eq, comparator_23_eq, comparator_24_eq, comparator_25_eq, comparator_26_eq,
       comparator_27_eq, comparator_28_eq, comparator_29_eq, comparator_30_eq, comparator_31_eq,
       comparator_32_eq, comparator_33_eq, comparator_34_eq, comparator_35_eq, comparator_36_eq,
       comparator_37_eq, comparator_38_eq, comparator_39_eq, comparator_40_eq, comparator_41_eq,
       comparator_42_eq, comparator_43_eq, comparator_44_eq, comparator_45_eq, comparator_46_eq,
       comparator_47_eq, comparator_48_eq, comparator_49_eq, comparator_50_eq, comparator_51_eq,
       comparator_52_eq, comparator_53_eq, comparator_54_eq, comparator_55_eq, comparator_56_eq,
       comparator_57_eq, comparator_58_eq, comparator_60_eq, comparator_61_eq, comparator_62_eq,
       comparator_63_eq, comparator_64_eq, comparator_65_eq, comparator_66_eq, comparator_67_eq,
       comparator_68_eq, if_lui, if_mul, if_mulh, if_mulhu, if_sra_i, if_sub, multiplexer_7_out, not_1_out,
       not_2_out, not_3_out, or_1_out, or_2_out, or_4_out, or_8_out, or_9_out, or_10_out, or_11_out;
  wire [1:0] multiplexer_15_out, multiplexer_16_out;
  wire [2:0] multiplexer_1_out, multiplexer_2_out, multiplexer_3_out, multiplexer_4_out;
  wire [3:0] multiplexer_6_out, multiplexer_10_out, multiplexer_11_out, multiplexer_12_out,
       multiplexer_13_out, multiplexer_14_out, multiplexer_17_out, multiplexer_19_out;

  Comparator #(.width(7)) comparator_1 (.a(inst[6:0]), .b(7'b0100011), .eq(comparator_1_eq));  // open: gt, lt
  Comparator #(.width(7)) comparator_2 (.a(inst[6:0]), .b(7'b1100011), .eq(comparator_2_eq));  // open: gt, lt
  Comparator #(.width(7)) comparator_3 (.a(inst[6:0]), .b(7'b0010111), .eq(comparator_3_eq));  // open: gt, lt
  Comparator #(.width(7)) comparator_4 (.a(inst[6:0]), .b(7'b0110111), .eq(comparator_4_eq));  // open: gt, lt
  Comparator #(.width(7)) comparator_5 (.a(inst[6:0]), .b(7'b1101111), .eq(comparator_5_eq));  // open: gt, lt
  Comparator #(.width(7)) comparator_6 (.a(inst[6:0]), .b(7'b1110011), .eq(comparator_6_eq));  // open: gt, lt
  Comparator #(.width(3)) comparator_7 (.a(inst[14:12]), .b(3'b101), .eq(comparator_7_eq));  // open: gt, lt
  Comparator #(.width(3)) comparator_8 (.a(inst[14:12]), .b(3'b000), .eq(comparator_8_eq));  // open: gt, lt
  Comparator #(.width(3)) comparator_9 (.a(inst[14:12]), .b(3'b001), .eq(comparator_9_eq));  // open: gt, lt
  Comparator #(.width(3)) comparator_10 (.a(inst[14:12]), .b(3'b100), .eq(comparator_10_eq));  // open: gt, lt
  Comparator #(.width(3)) comparator_11 (.a(inst[14:12]), .b(3'b110), .eq(comparator_11_eq));  // open: gt, lt
  Comparator #(.width(3)) comparator_12 (.a(inst[14:12]), .b(3'b101), .eq(comparator_12_eq));  // open: gt, lt
  Comparator #(.width(3)) comparator_13 (.a(inst[14:12]), .b(3'b111), .eq(comparator_13_eq));  // open: gt, lt
  or or_1 (or_1_out, comparator_3_eq, comparator_4_eq);
  not not_1 (not_1_out, BrEq);
  not not_2 (not_2_out, BrLt);
  not not_3 (not_3_out, BrLt);
  Multiplexer #(.enable("false"), .width(3)) multiplexer_1 (
    .in0(3'b000), .in1(3'b001), .out(multiplexer_1_out), .sel(comparator_1_eq));
  Multiplexer #(.enable("false"), .width(3)) multiplexer_2 (
    .in0(multiplexer_1_out), .in1(3'b010), .out(multiplexer_2_out), .sel(comparator_2_eq));
  Multiplexer #(.enable("false"), .width(3)) multiplexer_3 (
    .in0(multiplexer_2_out), .in1(3'b011), .out(multiplexer_3_out), .sel(or_1_out));
  Multiplexer #(.enable("false"), .width(3)) multiplexer_4 (
    .in0(multiplexer_3_out), .in1(3'b100), .out(multiplexer_4_out), .sel(comparator_5_eq));
  and and_1 (and_1_out, comparator_6_eq, comparator_7_eq);
  and and_2 (and_2_out, BrEq, comparator_8_eq);
  and and_3 (and_3_out, not_1_out, comparator_9_eq);
  and and_4 (and_4_out, BrLt, comparator_10_eq);
  and and_5 (and_5_out, BrLt, comparator_11_eq);
  and and_6 (and_6_out, not_2_out, comparator_12_eq);
  and and_7 (and_7_out, not_3_out, comparator_13_eq);
  Multiplexer #(.enable("false"), .width(3)) multiplexer_5 (
    .in0(multiplexer_4_out), .in1(3'b101), .out(ImmSel), .sel(and_1_out));
  or or_2 (or_2_out, and_2_out, and_3_out, and_4_out, and_5_out, and_6_out, and_7_out);
  Comparator #(.width(7)) comparator_14 (.a(inst[6:0]), .b(7'b1100011), .eq(comparator_14_eq));  // open: gt, lt
  Multiplexer #(.enable("false"), .select(2), .width(4)) multiplexer_6 (
    .in0(4'b0001), .in1(4'b0011), .in2(4'b1111), .out(multiplexer_6_out), .sel(inst[13:12]));  // open: in3
  Comparator #(.width(7)) comparator_15 (.a(inst[6:0]), .b(7'b1100111), .eq(comparator_15_eq));  // open: gt, lt
  Multiplexer #(.enable("false")) multiplexer_7 (
    .in0(1'b0), .in1(or_2_out), .out(multiplexer_7_out), .sel(comparator_14_eq));
  Comparator #(.width(7)) comparator_16 (.a(inst[6:0]), .b(7'b1101111), .eq(comparator_16_eq));  // open: gt, lt
  Comparator #(.width(7)) comparator_17 (.a(inst[6:0]), .b(7'b0100011), .eq(MemRW));  // open: gt, lt
  Multiplexer #(.enable("false"), .width(2)) multiplexer_8 (
    .in0(2'b00), .in1(inst[13:12]), .out(Load_Type), .sel(comparator_18_eq));
  Comparator #(.width(7)) comparator_18 (.a(inst[6:0]), .b(7'b0000011), .eq(comparator_18_eq));  // open: gt, lt
  Comparator #(.width(7)) comparator_19 (.a(inst[6:0]), .b(7'b1110011), .eq(CSRWen));  // open: gt, lt
  Comparator #(.width(3)) comparator_20 (.a(inst[14:12]), .b(3'b101), .eq(comparator_20_eq));  // open: gt, lt
  or or_3 (PCSel, comparator_15_eq, multiplexer_7_out, comparator_16_eq);
  Multiplexer #(.enable("false"), .width(4)) multiplexer_9 (
    .in0(4'b0000), .in1(multiplexer_6_out), .out(Write_Enable), .sel(MemRW));
  Comparator #(.width(7)) comparator_21 (.a(inst[6:0]), .b(7'b1100011), .eq(comparator_21_eq));  // open: gt, lt
  Comparator #(.width(3)) comparator_22 (.a(inst[14:12]), .b(3'b110), .eq(comparator_22_eq));  // open: gt, lt
  Comparator #(.width(3)) comparator_23 (.a(inst[14:12]), .b(3'b111), .eq(comparator_23_eq));  // open: gt, lt
  and and_8 (CSRSel, CSRWen, comparator_20_eq);
  or or_4 (or_4_out, comparator_22_eq, comparator_23_eq);
  and and_9 (BrUn, comparator_21_eq, or_4_out);
  Comparator #(.width(7)) comparator_24 (.a(inst[6:0]), .b(7'b0010111), .eq(comparator_24_eq));  // open: gt, lt
  Comparator #(.width(7)) comparator_25 (.a(inst[6:0]), .b(7'b1100011), .eq(comparator_25_eq));  // open: gt, lt
  Comparator #(.width(7)) comparator_26 (.a(inst[6:0]), .b(7'b1101111), .eq(comparator_26_eq));  // open: gt, lt
  Comparator #(.width(7)) comparator_27 (.a(inst[6:0]), .b(7'b0000011), .eq(comparator_27_eq));  // open: gt, lt
  Comparator #(.width(7)) comparator_28 (.a(inst[6:0]), .b(7'b0010011), .eq(comparator_28_eq));  // open: gt, lt
  Comparator #(.width(7)) comparator_29 (.a(inst[6:0]), .b(7'b0010111), .eq(comparator_29_eq));  // open: gt, lt
  Comparator #(.width(7)) comparator_30 (.a(inst[6:0]), .b(7'b0100011), .eq(comparator_30_eq));  // open: gt, lt
  Comparator #(.width(7)) comparator_31 (.a(inst[6:0]), .b(7'b0110111), .eq(comparator_31_eq));  // open: gt, lt
  Comparator #(.width(7)) comparator_32 (.a(inst[6:0]), .b(7'b1100011), .eq(comparator_32_eq));  // open: gt, lt
  Comparator #(.width(7)) comparator_33 (.a(inst[6:0]), .b(7'b1100111), .eq(comparator_33_eq));  // open: gt, lt
  Comparator #(.width(7)) comparator_34 (.a(inst[6:0]), .b(7'b1101111), .eq(comparator_34_eq));  // open: gt, lt
  Comparator #(.width(7)) comparator_35 (.a(inst[6:0]), .b(7'b0000011), .eq(comparator_35_eq));  // open: gt, lt
  Comparator #(.width(7)) comparator_36 (.a(inst[6:0]), .b(7'b0010011), .eq(comparator_36_eq));  // open: gt, lt
  Comparator #(.width(7)) comparator_37 (.a(inst[6:0]), .b(7'b0010111), .eq(comparator_37_eq));  // open: gt, lt
  Comparator #(.width(7)) comparator_38 (.a(inst[6:0]), .b(7'b0110011), .eq(comparator_38_eq));  // open: gt, lt
  Comparator #(.width(7)) comparator_39 (.a(inst[6:0]), .b(7'b0110111), .eq(comparator_39_eq));  // open: gt, lt
  Comparator #(.width(7)) comparator_40 (.a(inst[6:0]), .b(7'b1100111), .eq(comparator_40_eq));  // open: gt, lt
  Comparator #(.width(7)) comparator_41 (.a(inst[6:0]), .b(7'b1101111), .eq(comparator_41_eq));  // open: gt, lt
  Comparator #(.width(7)) comparator_42 (.a(inst[6:0]), .b(7'b1110011), .eq(comparator_42_eq));  // open: gt, lt
  Multiplexer #(.enable("false"), .select(3), .width(4)) multiplexer_10 (
    .in0(4'b0000), .in1(4'b0001), .in2(4'b0010), .in4(4'b0100), .in5(4'b0101), .in6(4'b0110), .in7(4'b0111),
    .out(multiplexer_10_out), .sel(inst[14:12]));  // open: in3
  Comparator #(.width(7)) comparator_43 (.a(inst[6:0]), .b(7'b0110011), .eq(comparator_43_eq));  // open: gt, lt
  Comparator #(.width(3)) comparator_44 (.a(inst[14:12]), .b(3'b000), .eq(comparator_44_eq));  // open: gt, lt
  Comparator #(.width(7)) comparator_45 (.a(inst[31:25]), .b(7'b0000001), .eq(comparator_45_eq));  // open: gt, lt
  Comparator #(.width(7)) comparator_46 (.a(inst[6:0]), .b(7'b0110011), .eq(comparator_46_eq));  // open: gt, lt
  Comparator #(.width(3)) comparator_47 (.a(inst[14:12]), .b(3'b000), .eq(comparator_47_eq));  // open: gt, lt
  Comparator #(.width(7)) comparator_48 (.a(inst[31:25]), .b(7'b0100000), .eq(comparator_48_eq));  // open: gt, lt
  Comparator #(.width(7)) comparator_49 (.a(inst[6:0]), .b(7'b0110011), .eq(comparator_49_eq));  // open: gt, lt
  Comparator #(.width(3)) comparator_50 (.a(inst[14:12]), .b(3'b001), .eq(comparator_50_eq));  // open: gt, lt
  Comparator #(.width(7)) comparator_51 (.a(inst[31:25]), .b(7'b0000001), .eq(comparator_51_eq));  // open: gt, lt
  Comparator #(.width(7)) comparator_52 (.a(inst[6:0]), .b(7'b0110011), .eq(comparator_52_eq));  // open: gt, lt
  Comparator #(.width(3)) comparator_53 (.a(inst[14:12]), .b(3'b011), .eq(comparator_53_eq));  // open: gt, lt
  Comparator #(.width(7)) comparator_54 (.a(inst[31:25]), .b(7'b0000001), .eq(comparator_54_eq));  // open: gt, lt
  or or_5 (ASel, comparator_24_eq, comparator_25_eq, comparator_26_eq);
  and and_10 (if_mul, comparator_43_eq, and_11_out);
  and and_11 (and_11_out, comparator_44_eq, comparator_45_eq);
  and and_12 (if_sub, comparator_46_eq, and_13_out);
  and and_13 (and_13_out, comparator_47_eq, comparator_48_eq);
  and and_14 (if_mulh, comparator_49_eq, and_15_out);
  and and_15 (and_15_out, comparator_50_eq, comparator_51_eq);
  and and_16 (if_mulhu, comparator_52_eq, and_17_out);
  and and_17 (and_17_out, comparator_53_eq, comparator_54_eq);
  or or_6 (RegWEn, comparator_35_eq, comparator_36_eq, comparator_37_eq, comparator_38_eq, comparator_39_eq, comparator_40_eq, comparator_41_eq, comparator_42_eq);
  Multiplexer #(.enable("false"), .width(4)) multiplexer_11 (
    .in0(multiplexer_10_out), .in1(4'b1000), .out(multiplexer_11_out), .sel(if_mul));
  or or_7 (BSel, comparator_27_eq, comparator_28_eq, comparator_29_eq, comparator_30_eq, comparator_31_eq, comparator_32_eq, comparator_33_eq, comparator_34_eq);
  Multiplexer #(.enable("false"), .width(4)) multiplexer_12 (
    .in0(multiplexer_11_out), .in1(4'b1100), .out(multiplexer_12_out), .sel(if_sub));
  Multiplexer #(.enable("false"), .width(4)) multiplexer_13 (
    .in0(multiplexer_12_out), .in1(4'b1001), .out(multiplexer_13_out), .sel(if_mulh));
  Comparator #(.width(7)) comparator_55 (.a(inst[6:0]), .b(7'b0110011), .eq(comparator_55_eq));  // open: gt, lt
  Comparator #(.width(7)) comparator_56 (.a(inst[6:0]), .b(7'b0010011), .eq(comparator_56_eq));  // open: gt, lt
  Comparator #(.width(3)) comparator_57 (.a(inst[14:12]), .b(3'b101), .eq(comparator_57_eq));  // open: gt, lt
  Comparator #(.width(7)) comparator_58 (.a(inst[31:25]), .b(7'b0100000), .eq(comparator_58_eq));  // open: gt, lt
  Multiplexer #(.enable("false"), .width(4)) multiplexer_14 (
    .in0(multiplexer_13_out), .in1(4'b1011), .out(multiplexer_14_out), .sel(if_mulhu));
  or or_8 (or_8_out, comparator_55_eq, comparator_56_eq);
  and and_18 (and_18_out, comparator_57_eq, comparator_58_eq);
  Comparator #(.width(7)) comparator_59 (.a(inst[6:0]), .b(7'b0110111), .eq(if_lui));  // open: gt, lt
  Comparator #(.width(7)) comparator_60 (.a(inst[6:0]), .b(7'b0010011), .eq(comparator_60_eq));  // open: gt, lt
  Comparator #(.width(7)) comparator_61 (.a(inst[6:0]), .b(7'b0010111), .eq(comparator_61_eq));  // open: gt, lt
  Comparator #(.width(7)) comparator_62 (.a(inst[6:0]), .b(7'b0110011), .eq(comparator_62_eq));  // open: gt, lt
  Comparator #(.width(7)) comparator_63 (.a(inst[6:0]), .b(7'b0110111), .eq(comparator_63_eq));  // open: gt, lt
  Comparator #(.width(7)) comparator_64 (.a(inst[6:0]), .b(7'b1100111), .eq(comparator_64_eq));  // open: gt, lt
  Comparator #(.width(7)) comparator_65 (.a(inst[6:0]), .b(7'b1101111), .eq(comparator_65_eq));  // open: gt, lt
  Comparator #(.width(7)) comparator_66 (.a(inst[6:0]), .b(7'b1110011), .eq(comparator_66_eq));  // open: gt, lt
  Comparator #(.width(7)) comparator_67 (.a(inst[6:0]), .b(7'b0110011), .eq(comparator_67_eq));  // open: gt, lt
  Comparator #(.width(7)) comparator_68 (.a(inst[6:0]), .b(7'b0010011), .eq(comparator_68_eq));  // open: gt, lt
  and and_19 (if_sra_i, or_8_out, and_18_out);
  or or_9 (or_9_out, comparator_60_eq, comparator_61_eq, comparator_62_eq, comparator_63_eq);
  Multiplexer #(.enable("false"), .width(2)) multiplexer_15 (
    .in0(2'b00), .in1(2'b01), .out(multiplexer_15_out), .sel(or_9_out));
  Multiplexer #(.enable("false"), .width(2)) multiplexer_16 (
    .in0(multiplexer_15_out), .in1(2'b10), .out(multiplexer_16_out), .sel(or_10_out));
  or or_10 (or_10_out, comparator_64_eq, comparator_65_eq);
  Multiplexer #(.enable("false"), .width(4)) multiplexer_17 (
    .in0(multiplexer_14_out), .in1(4'b1101), .out(multiplexer_17_out), .sel(if_sra_i));
  or or_11 (or_11_out, comparator_67_eq, comparator_68_eq);
  Multiplexer #(.enable("false"), .width(2)) multiplexer_18 (
    .in0(multiplexer_16_out), .in1(2'b11), .out(WBSel), .sel(comparator_66_eq));
  Multiplexer #(.enable("false"), .width(4)) multiplexer_19 (
    .in0(4'b0000), .in1(multiplexer_17_out), .out(multiplexer_19_out), .sel(or_11_out));
  Multiplexer #(.enable("false"), .width(4)) multiplexer_20 (
    .in0(multiplexer_19_out), .in1(4'b1111), .out(ALUSel), .sel(if_lui));

  // Other names for the same wires on the sheet: opcode[6:0] = inst[6:0]; rd[4:0] = inst[11:7];
  //   funct3[2:0] = inst[14:12]; rs1[4:0] = inst[19:15]; rs2[4:0] = inst[24:20]; funct7[6:0] = inst[31:25];
  //   LoadType[1:0] = Load_Type

  // Notes on the sheet:
  //   INPUTS to your circuit
  //   DON'T CHANGE THE LOCATIONS OF THE INPUTS AND OUTPUTS!
  //   OUTPUT from your circuit
endmodule
