// Logisim project cpu.circ as structural Verilog: 1 circuit, main circuit cpu
module cpu (
  input  clk,
  input  [31:0] INSTRUCTION,
  input  [31:0] READ_DATA,
  output [31:0] WRITE_ADDRESS,
  output [31:0] PROGRAM_COUNTER,
  output [31:0] ra,
  output [31:0] sp,
  output [31:0] t0,
  output [31:0] t1,
  output [31:0] t2,
  output [31:0] s0,
  output [31:0] s1,
  output [31:0] a0,
  output [31:0] tohost,
  output [3:0] WRITE_ENABLE,
  output [31:0] WRITE_DATA
);

  wire ASel, BrEq, BrLt, BrUn, BSel, CSRSel, CSRWen, MemRW, PCSel, RegWEn;
  wire [0:0] PC_q;
  wire [1:0] Load_Type, WBSel;
  wire [2:0] funct3, ImmSel;
  wire [3:0] ALUSel, WE_Raw;
  wire [4:0] bit_extender_1_out, bit_extender_2_out, multiplier_1_out, multiplier_2_out;
  wire [6:0] funct7;
  wire [24:0] INST_EXT;
  wire [31:0] adder_1_out, adder_2_out, bit_extender_3_out, bit_extender_4_out, Imm_Generated,
       multiplexer_1_out, multiplexer_2_out, multiplexer_3_out, multiplexer_4_out, multiplexer_5_out, PC_EXT,
       Processed_Data, RD_1, RD_2, shifter_3_out, Write_Data_t;

  Adder #(.width(32)) adder_1 (.a({PROGRAM_COUNTER[31:1], PC_q[0]}), .b(32'h4), .out(adder_1_out));  // open: cin, cout
  Multiplexer #(.enable("false"), .width(32)) multiplexer_1 (
    .in0(adder_1_out), .in1(WRITE_ADDRESS), .out(multiplexer_1_out), .sel(PCSel));
  Register #(.width(32)) PC (.D(multiplexer_1_out), .clk(clk), .Q({PROGRAM_COUNTER[31:1], PC_q[0]}));  // open: en, clr
  Multiplexer #(.enable("false"), .width(32)) multiplexer_2 (
    .in0(INSTRUCTION), .in1(32'h13), .out(multiplexer_2_out), .sel(PCSel));
  Register #(.width(32)) register_1 (.D({PROGRAM_COUNTER[31:1], 1'b0}), .clk(clk), .Q(PC_EXT));  // open: en, clr
  Register #(.width(32)) register_2 (
    .D(multiplexer_2_out), .clk(clk), .Q({funct7, INST_EXT[24:15], funct3, INST_EXT[11:0]}));  // open: en, clr
  control_logic control_logic_1 (
    .CSRWen(CSRWen), .Write_Enable(WE_Raw), .Load_Type(Load_Type), .PCSel(PCSel), .RegWEn(RegWEn),
    .ImmSel(ImmSel), .BrUn(BrUn), .ASel(ASel), .BSel(BSel), .ALUSel(ALUSel), .MemRW(MemRW), .WBSel(WBSel),
    .CSRSel(CSRSel), .inst({funct7, INST_EXT[24:15], funct3, INST_EXT[11:0]}), .BrEq(BrEq), .BrLt(BrLt));
  imm_gen imm_gen_1 (.inst({funct7, INST_EXT[24:15], funct3, INST_EXT[11:0]}), .ImmSel(ImmSel), .imm(Imm_Generated));
  regfile regfile_1 (
    .rs1(INST_EXT[19:15]), .rs2(INST_EXT[24:20]), .rd(INST_EXT[11:7]), .Write_Data(Write_Data_t),
    .RegWEn(RegWEn), .clk(clk), .ra(ra), .sp(sp), .t0(t0), .t1(t1), .t2(t2), .s0(s0), .s1(s1), .a0(a0),
    .Read_Data_1(RD_1), .Read_Data_2(RD_2));
  Multiplexer #(.enable("false"), .width(32)) multiplexer_3 (
    .in0(RD_1), .in1(Imm_Generated), .out(multiplexer_3_out), .sel(CSRSel));
  Shifter #(.width(4)) shifter_1 (.in(WE_Raw), .\dist (WRITE_ADDRESS[1:0]), .out(WRITE_ENABLE));
  Multiplexer #(.enable("false"), .width(32)) multiplexer_4 (
    .in0(RD_1), .in1(PC_EXT), .out(multiplexer_4_out), .sel(ASel));
  Multiplexer #(.enable("false"), .width(32)) multiplexer_5 (
    .in0(RD_2), .in1(Imm_Generated), .out(multiplexer_5_out), .sel(BSel));
  branch_comp branch_comp_1 (.rs1(RD_1), .rs2(RD_2), .BrUn(BrUn), .BrEq(BrEq), .BrLt(BrLt));
  alu alu_1 (.Result(WRITE_ADDRESS), .A(multiplexer_4_out), .B(multiplexer_5_out), .ALUSel(ALUSel));
  // csr csr_1: pin names not known; wires that end beside it: {funct7, INST_EXT[24:20]}, multiplexer_3_out, CSRWen, clk, tohost
  assign bit_extender_1_out = {{3{1'b0}}, WRITE_ADDRESS[1:0]};  // Bit_Extender bit_extender_1
  Adder #(.width(32)) adder_2 (.a(PC_EXT), .b(32'h4), .out(adder_2_out));  // open: cin, cout
  Multiplier #(.width(5)) multiplier_1 (
    .a(5'b01000), .b(bit_extender_1_out), .out(multiplier_1_out));  // open: cin, cout
  assign bit_extender_2_out = {{3{1'b0}}, WRITE_ADDRESS[1:0]};  // Bit_Extender bit_extender_2
  Shifter #(.width(32)) shifter_2 (.in(RD_2), .\dist (multiplier_1_out), .out(WRITE_DATA));
  Multiplier #(.width(5)) multiplier_2 (
    .a(5'b01000), .b(bit_extender_2_out), .out(multiplier_2_out));  // open: cin, cout
  Multiplexer #(.enable("false"), .select(2), .width(32)) multiplexer_6 (
    .in0(Processed_Data), .in1(WRITE_ADDRESS), .in2(adder_2_out), .in3(tohost), .out(Write_Data_t),
    .sel(WBSel));
  Shifter #(.shift("lr"), .width(32)) shifter_3 (.in(READ_DATA), .\dist (multiplier_2_out), .out(shifter_3_out));
  assign bit_extender_3_out = {{24{shifter_3_out[7]}}, shifter_3_out[7:0]};  // Bit_Extender bit_extender_3
  assign bit_extender_4_out = {{16{shifter_3_out[15]}}, shifter_3_out[15:0]};  // Bit_Extender bit_extender_4
  Multiplexer #(.enable("false"), .select(2), .width(32)) multiplexer_7 (
    .in0(bit_extender_3_out), .in1(bit_extender_4_out), .in2(shifter_3_out), .out(Processed_Data),
    .sel(Load_Type));  // open: in3

  assign PROGRAM_COUNTER[0] = 1'b0;

  // Other names for the same wires on the sheet: ALU_Result[31:0] = WRITE_ADDRESS; opcode[6:0] = INST_EXT[6:0];
  //   rd[4:0] = INST_EXT[11:7]; INST_EXT (some bits) = {funct7, funct3}; rs1[4:0] = INST_EXT[19:15];
  //   rs2[4:0] = INST_EXT[24:20]

  // Notes on the sheet:
  //   Output to IMEM
  //   IMEM (do **NOT** move this)
  //   Inputs from IMEM
  //   It is OK to move the PC, RegFile, ALU, MEM, Branch Comp, Imm Gen, and Control Logic to wherever is most convenient for you when constructing your CPU, and to delete this text
  //   Inputs/Outputs for testing. Do **NOT** move these.
  //   Outputs To DMEM
  //   DMEM (do **NOT** move this)
  //   Inputs From DMEM
  //   0 - lb, 1 - lh, 2 - lw, 3 - und
endmodule
