// Logisim project regfile.circ as structural Verilog: 1 circuit, main circuit regfile
module regfile (
  input  [4:0] rs1,
  input  [4:0] rs2,
  input  [4:0] rd,
  input  [31:0] Write_Data,
  input  RegWEn,
  input  clk,
  output [31:0] ra,
  output [31:0] sp,
  output [31:0] t0,
  output [31:0] t1,
  output [31:0] t2,
  output [31:0] s0,
  output [31:0] s1,
  output [31:0] a0,
  output [31:0] Read_Data_1,
  output [31:0] Read_Data_2
);

  wire WE_0, WE_1, WE_2, WE_3, WE_4, WE_5, WE_6, WE_7, WE_8, WE_9, WE_10, WE_11, WE_12, WE_13, WE_14, WE_15,
       WE_16, WE_17, WE_18, WE_19, WE_20, WE_21, WE_22, WE_23, WE_24, WE_25, WE_26, WE_27, WE_28, WE_29,
       WE_30, WE_31;
  wire [31:0] x3, x4, x11, x12, x13, x14, x15, x16, x17, x18, x19, x20, x21, x22, x23, x24, x25, x26, x27,
       x28, x29, x30, x31;

  Register #(.width(32)) register_1 (.D(Write_Data), .en(WE_1), .clk(clk), .Q(ra));  // open: clr
  Register #(.width(32)) register_2 (.D(Write_Data), .en(WE_2), .clk(clk), .Q(sp));  // open: clr
  Register #(.width(32)) register_3 (.D(Write_Data), .en(WE_3), .clk(clk), .Q(x3));  // open: clr
  Register #(.width(32)) register_4 (.D(Write_Data), .en(WE_4), .clk(clk), .Q(x4));  // open: clr
  Demultiplexer #(.enable("false"), .select(5)) demultiplexer_1 (
    .out0(WE_0), .out1(WE_1), .out2(WE_2), .out3(WE_3), .out4(WE_4), .out5(WE_5), .out6(WE_6), .out7(WE_7),
    .out8(WE_8), .out9(WE_9), .out10(WE_10), .out11(WE_11), .out12(WE_12), .out13(WE_13), .out14(WE_14),
    .out15(WE_15), .out16(WE_16), .out17(WE_17), .out18(WE_18), .out19(WE_19), .out20(WE_20), .out21(WE_21),
    .out22(WE_22), .out23(WE_23), .out24(WE_24), .out25(WE_25), .out26(WE_26), .out27(WE_27), .out28(WE_28),
    .out29(WE_29), .out30(WE_30), .out31(WE_31), .in(RegWEn), .sel(rd));
  Register #(.width(32)) register_5 (.D(Write_Data), .en(WE_5), .clk(clk), .Q(t0));  // open: clr
  Register #(.width(32)) register_6 (.D(Write_Data), .en(WE_6), .clk(clk), .Q(t1));  // open: clr
  Register #(.width(32)) register_7 (.D(Write_Data), .en(WE_7), .clk(clk), .Q(t2));  // open: clr
  Register #(.width(32)) register_8 (.D(Write_Data), .en(WE_8), .clk(clk), .Q(s0));  // open: clr
  Register #(.width(32)) register_9 (.D(Write_Data), .en(WE_9), .clk(clk), .Q(s1));  // open: clr
  Register #(.width(32)) register_10 (.D(Write_Data), .en(WE_10), .clk(clk), .Q(a0));  // open: clr
  Register #(.width(32)) register_11 (.D(Write_Data), .en(WE_11), .clk(clk), .Q(x11));  // open: clr
  Register #(.width(32)) register_12 (.D(Write_Data), .en(WE_12), .clk(clk), .Q(x12));  // open: clr
  Register #(.width(32)) register_13 (.D(Write_Data), .en(WE_13), .clk(clk), .Q(x13));  // open: clr
  Register #(.width(32)) register_14 (.D(Write_Data), .en(WE_14), .clk(clk), .Q(x14));  // open: clr
  Register #(.width(32)) register_15 (.D(Write_Data), .en(WE_15), .clk(clk), .Q(x15));  // open: clr
  Register #(.width(32)) register_16 (.D(Write_Data), .en(WE_16), .clk(clk), .Q(x16));  // open: clr
  Multiplexer #(.enable("false"), .select(5), .width(32)) multiplexer_1 (
    .in0({32{1'b0}}), .in1(ra), .in2(sp), .in3(x3), .in4(x4), .in5(t0), .in6(t1), .in7(t2), .in8(s0),
    .in9(s1), .in10(a0), .in11(x11), .in12(x12), .in13(x13), .in14(x14), .in15(x15), .in16(x16), .in17(x17),
    .in18(x18), .in19(x19), .in20(x20), .in21(x21), .in22(x22), .in23(x23), .in24(x24), .in25(x25),
    .in26(x26), .in27(x27), .in28(x28), .in29(x29), .in30(x30), .in31(x31), .out(Read_Data_1), .sel(rs1));
  Register #(.width(32)) register_17 (.D(Write_Data), .en(WE_17), .clk(clk), .Q(x17));  // open: clr
  Register #(.width(32)) register_18 (.D(Write_Data), .en(WE_18), .clk(clk), .Q(x18));  // open: clr
  Register #(.width(32)) register_19 (.D(Write_Data), .en(WE_19), .clk(clk), .Q(x19));  // open: clr
  Register #(.width(32)) register_20 (.D(Write_Data), .en(WE_20), .clk(clk), .Q(x20));  // open: clr
  Register #(.width(32)) register_21 (.D(Write_Data), .en(WE_21), .clk(clk), .Q(x21));  // open: clr
  Register #(.width(32)) register_22 (.D(Write_Data), .en(WE_22), .clk(clk), .Q(x22));  // open: clr
  Register #(.width(32)) register_23 (.D(Write_Data), .en(WE_23), .clk(clk), .Q(x23));  // open: clr
  Register #(.width(32)) register_24 (.D(Write_Data), .en(WE_24), .clk(clk), .Q(x24));  // open: clr
  Multiplexer #(.enable("false"), .select(5), .width(32)) multiplexer_2 (
    .in0({32{1'b0}}), .in1(ra), .in2(sp), .in3(x3), .in4(x4), .in5(t0), .in6(t1), .in7(t2), .in8(s0),
    .in9(s1), .in10(a0), .in11(x11), .in12(x12), .in13(x13), .in14(x14), .in15(x15), .in16(x16), .in17(x17),
    .in18(x18), .in19(x19), .in20(x20), .in21(x21), .in22(x22), .in23(x23), .in24(x24), .in25(x25),
    .in26(x26), .in27(x27), .in28(x28), .in29(x29), .in30(x30), .in31(x31), .out(Read_Data_2), .sel(rs2));
  Register #(.width(32)) register_25 (.D(Write_Data), .en(WE_25), .clk(clk), .Q(x25));  // open: clr
  Register #(.width(32)) register_26 (.D(Write_Data), .en(WE_26), .clk(clk), .Q(x26));  // open: clr
  Register #(.width(32)) register_27 (.D(Write_Data), .en(WE_27), .clk(clk), .Q(x27));  // open: clr
  Register #(.width(32)) register_28 (.D(Write_Data), .en(WE_28), .clk(clk), .Q(x28));  // open: clr
  Register #(.width(32)) register_29 (.D(Write_Data), .en(WE_29), .clk(clk), .Q(x29));  // open: clr
  Register #(.width(32)) register_30 (.D(Write_Data), .en(WE_30), .clk(clk), .Q(x30));  // open: clr
  Register #(.width(32)) register_31 (.D(Write_Data), .en(WE_31), .clk(clk), .Q(x31));  // open: clr

  // Other names for the same wires on the sheet: read_data1[31:0] = Read_Data_1; read_data2[31:0] = Read_Data_2;
  //   read_reg1[4:0] = rs1; read_reg2[4:0] = rs2; write_en = RegWEn; write_reg[4:0] = rd; x1[31:0] = ra;
  //   x2[31:0] = sp; x5[31:0] = t0; x6[31:0] = t1; x7[31:0] = t2; x8[31:0] = s0; x9[31:0] = s1; x10[31:0] = a0

  // Notes on the sheet:
  //   INPUTS to your circuit
  //   DON'T CHANGE THE LOCATIONS OF THE INPUTS AND OUTPUTS!
  //   These are DEBUG/TEST outputs from your circuit.
  //   OUTPUTS from your circuit
endmodule
